// Digital circuit Acc8-seq.dig as structural Verilog
module Acc8_seq (
  input  EN,
  input  RST,
  input  CLK,
  output [7:0] R,
  output OVF
);

  wire [3:0] counter_1_out;
  wire [7:0] rom_1_d;

  Counter #(.Bits(4)) counter_1 (.en(EN), .C(CLK), .clr(RST), .out(counter_1_out));  // open: ovf
  ROM #(.AddrBits(4), .Bits(8)) rom_1 (.A(counter_1_out), .sel(EN), .D(rom_1_d));
  Acc8 acc8_1 (.A(rom_1_d), .EN(EN), .RST(RST), .CLK(CLK), .R(R), .OVF(OVF));

  // Notes on the sheet:
  //   contents of rom_1 (hex, n*v repeats v):
  //   1,2,3,4,5,6,7,8,9,10,11,12,13,14,15,16
endmodule
