// Digital circuit Acc8-seq_Telmo.dig as structural Verilog
module Acc8_seq_Telmo (
  input  EN,
  input  RST,
  input  CLK,
  output [7:0] R,
  output OVF
);

  wire and_1_out, comparator_1_eq, comparator_2_lt, counter_1_ovf, nor_1_out;
  wire [3:0] counter_1_out;
  wire [7:0] rom_1_d;

  Counter #(.Bits(4)) counter_1 (.en(EN), .C(CLK), .clr(RST), .out(counter_1_out), .ovf(counter_1_ovf));
  ROM #(.AddrBits(4), .Bits(8)) rom_1 (.A(counter_1_out), .sel(EN), .D(rom_1_d));
  Comparator #(.Bits(8)) comparator_1 (.a(rom_1_d), .b(8'h55), .eq(comparator_1_eq));  // open: gt, lt
  Comparator #(.Bits(8)) comparator_2 (.a(rom_1_d), .b({8{1'b0}}), .lt(comparator_2_lt));  // open: gt, eq
  nor nor_1 (nor_1_out, comparator_1_eq, comparator_2_lt);
  and and_1 (and_1_out, EN, nor_1_out);
  Acc8 acc8_1 (.A(rom_1_d), .EN(and_1_out), .RST(RST), .CLK(CLK), .R(R), .OVF(OVF));

  // Notes on the sheet:
  //   contents of rom_1 (hex, n*v repeats v):
  //   1,2,4,25,5,a6,0,2b,c1,9,21,76,f2
endmodule
