// Digital circuit Acc8.dig as structural Verilog
module Acc8 (
  input  [7:0] A,
  input  EN,
  input  RST,
  input  CLK,
  output [7:0] R,
  output OVF
);

  wire and_1_out, not_1_out, xor_1_out;
  wire [7:0] reg8_1_p5;

  not not_1 (not_1_out, OVF);
  xor xor_1 (xor_1_out, CLK, CLK);
  and and_1 (and_1_out, EN, not_1_out);
  // Reg8 reg8_1: pin names not known; wires that end beside it: CLK, R, RST, and_1_out, reg8_1_p5
  AddSub8_ovf addsub8_ovf_1 (.A(A), .B(reg8_1_p5), .AS(xor_1_out), .S(R), .OVF(OVF));
endmodule
