// Digital circuit Add8.dig as structural Verilog
module Add8 (
  input  [7:0] A,
  input  [7:0] B,
  input  Ci,
  output [7:0] S
);

  wire fa_1_p5, fa_2_p5, fa_3_p5, fa_4_p5, fa_5_p5, fa_6_p5, fa_7_p5;

  // FA fa_1: pin names not known; wires that end beside it: A[0], B[0], Ci, S[0], fa_1_p5
  // FA fa_2: pin names not known; wires that end beside it: A[1], B[1], fa_1_p5, S[1], fa_2_p5
  // FA fa_3: pin names not known; wires that end beside it: A[2], B[2], fa_2_p5, S[2], fa_3_p5
  // FA fa_4: pin names not known; wires that end beside it: A[3], B[3], fa_3_p5, S[3], fa_4_p5
  // FA fa_5: pin names not known; wires that end beside it: A[4], B[4], fa_4_p5, S[4], fa_5_p5
  // FA fa_6: pin names not known; wires that end beside it: A[5], B[5], fa_5_p5, S[5], fa_6_p5
  // FA fa_7: pin names not known; wires that end beside it: A[6], B[6], fa_6_p5, S[6], fa_7_p5
  // FA fa_8: pin names not known; wires that end beside it: A[7], B[7], fa_7_p5, S[7]
endmodule
