// Digital circuit AddSub8-ovf.dig as structural Verilog
module AddSub8_ovf (
  input  [7:0] A,
  input  [7:0] B,
  input  AS,
  output [7:0] S,
  output OVF
);

  AddSub8 addsub8_1 (.A(A), .B(B), .AS(AS), .S(S));
  // det_ovf det_ovf_1: pin names not known; wires that end beside it: AS, A[7], B[7], S[7], OVF
endmodule
