// Digital circuit AddSub8.dig as structural Verilog
module AddSub8 (
  input  [7:0] A,
  input  [7:0] B,
  input  AS,
  output [7:0] S
);

  wire [7:0] xor_1_out;

  assign xor_1_out = B ^ {8{AS}};  // XOr xor_1, 8 bits wide
  Add8 add8_1 (.A(A), .B(xor_1_out), .Ci(AS), .S(S));
endmodule
