// Digital circuit det111.dig as structural Verilog
module det111 (
  input  In,
  input  CLK,
  output Out
);

  wire d_ff_1_q, d_ff_2_q, d_ff_3_q;

  D_FF d_ff_1 (.D(In), .C(CLK), .Q(d_ff_1_q));  // open: nQ
  D_FF d_ff_2 (.D(d_ff_1_q), .C(CLK), .Q(d_ff_2_q));  // open: nQ
  D_FF d_ff_3 (.D(d_ff_2_q), .C(CLK), .Q(d_ff_3_q));  // open: nQ
  and and_1 (Out, d_ff_3_q, d_ff_2_q, d_ff_1_q);
endmodule
