// Digital circuit reg4.dig as structural Verilog
module reg4 (
  input  [3:0] Din,
  input  EN,
  input  CLK,
  output [3:0] Dout
);

  wire and_1_out, and_2_out, and_3_out, and_4_out;

  and and_1 (and_1_out, CLK, EN);
  and and_2 (and_2_out, CLK, EN);
  and and_3 (and_3_out, CLK, EN);
  and and_4 (and_4_out, CLK, EN);
  D_FF FF0 (.D(Din[0]), .C(and_1_out), .Q(Dout[0]));  // open: nQ
  D_FF FF1 (.D(Din[1]), .C(and_2_out), .Q(Dout[1]));  // open: nQ
  D_FF FF2 (.D(Din[2]), .C(and_3_out), .Q(Dout[2]));  // open: nQ
  D_FF FF3 (.D(Din[3]), .C(and_4_out), .Q(Dout[3]));  // open: nQ
endmodule
